// Logisim project carry look ahead adder.circ as structural Verilog: 7 circuits, main circuit main
module _16_Bit_carry_look_ahead_adder (
  input  in_1,
  input  [15:0] Input_A,
  input  [15:0] Input_B,
  output [15:0] out_4,
  output OverFlow_Error
);

  wire carry_adder_with_nice_input_output_1_carry_out, carry_adder_with_nice_input_output_2_carry_out,
       carry_adder_with_nice_input_output_3_carry_out;

  Carry_adder_with_nice_input_output carry_adder_with_nice_input_output_1 (
    .Input_A(Input_A[3:0]), .Input_B(Input_B[3:0]), .Carry_In(in_1),
    .Carry_Out(carry_adder_with_nice_input_output_1_carry_out), .Output(out_4[3:0]));
  Carry_adder_with_nice_input_output carry_adder_with_nice_input_output_2 (
    .Input_A(Input_A[7:4]), .Input_B(Input_B[7:4]),
    .Carry_In(carry_adder_with_nice_input_output_1_carry_out),
    .Carry_Out(carry_adder_with_nice_input_output_2_carry_out), .Output(out_4[7:4]));
  Carry_adder_with_nice_input_output carry_adder_with_nice_input_output_3 (
    .Input_A(Input_A[11:8]), .Input_B(Input_B[11:8]),
    .Carry_In(carry_adder_with_nice_input_output_2_carry_out),
    .Carry_Out(carry_adder_with_nice_input_output_3_carry_out), .Output(out_4[11:8]));
  Carry_adder_with_nice_input_output carry_adder_with_nice_input_output_4 (
    .Input_A(Input_A[15:12]), .Input_B(Input_B[15:12]),
    .Carry_In(carry_adder_with_nice_input_output_3_carry_out), .Carry_Out(OverFlow_Error),
    .Output(out_4[15:12]));
endmodule

module _4_Bit_Carry_Adder (
  input  Carry_In,
  input  Input_A1,
  input  Input_B1,
  input  Input_A2,
  input  Input_B2,
  input  Input_A3,
  input  Input_B3,
  input  Input_A4,
  input  Input_B4,
  output out_10,
  output out_11,
  output out_12,
  output out_13,
  output out_14
);

  wire and_1_out, and_2_out, and_3_out, and_4_out, and_5_out, and_6_out, and_7_out, and_8_out, and_9_out,
       and_10_out, and_11_out, and_12_out, and_13_out, and_14_out, nand_1_out, nand_2_out, nand_3_out,
       nand_4_out, nor_1_out, nor_2_out, nor_3_out, nor_4_out, nor_5_out, nor_6_out, nor_7_out, not_1_out,
       not_2_out, not_3_out, not_4_out, not_5_out, not_6_out;

  nand nand_1 (nand_1_out, Input_A1, Input_B1);
  nor nor_1 (nor_1_out, Input_A2, Input_B2);
  nand nand_2 (nand_2_out, Input_A2, Input_B2);
  nor nor_2 (nor_2_out, Input_A3, Input_B3);
  nand nand_3 (nand_3_out, Input_A3, Input_B3);
  nor nor_3 (nor_3_out, Input_A4, Input_B4);
  nand nand_4 (nand_4_out, Input_A4, Input_B4);
  not not_1 (not_1_out, Carry_In);
  nor nor_4 (nor_4_out, Input_A1, Input_B1);
  not not_2 (not_2_out, nor_4_out);
  not not_3 (not_3_out, nor_1_out);
  not not_4 (not_4_out, nor_2_out);
  not not_5 (not_5_out, nor_3_out);
  not not_6 (not_6_out, not_1_out);
  and and_1 (and_1_out, not_2_out, nand_1_out);
  and and_2 (and_2_out, not_1_out, nand_1_out);
  and and_3 (and_3_out, not_3_out, nand_2_out);
  and and_4 (and_4_out, not_1_out, nand_1_out, nand_2_out);
  and and_5 (and_5_out, nand_2_out, nor_4_out);
  and and_6 (and_6_out, not_4_out, nand_3_out);
  and and_7 (and_7_out, not_1_out, nand_1_out, nand_2_out, nand_3_out);
  and and_8 (and_8_out, nand_2_out, nand_3_out, nor_1_out);
  and and_9 (and_9_out, nand_3_out, nor_1_out);
  and and_10 (and_10_out, not_5_out, nand_4_out);
  and and_11 (and_11_out, not_1_out, nand_1_out, nand_2_out, nand_3_out, nand_4_out);
  and and_12 (and_12_out, nand_2_out, nand_3_out, nor_3_out, nor_4_out);
  and and_13 (and_13_out, nand_3_out, nand_4_out, nor_1_out);
  and and_14 (and_14_out, nand_4_out, nor_2_out);
  nor nor_5 (nor_5_out, and_2_out, nor_4_out);
  nor nor_6 (nor_6_out, and_4_out, and_5_out, nor_1_out);
  xor xor_1 (out_10, not_6_out, and_1_out);
  xor xor_2 (out_11, nor_5_out, and_3_out);
  xor xor_3 (out_12, nor_6_out, and_6_out);
  nor nor_7 (nor_7_out, and_7_out, and_8_out, and_9_out, nor_2_out);
  xor xor_4 (out_13, nor_7_out, and_10_out);
  nor nor_8 (out_14, and_11_out, and_12_out, and_13_out, and_14_out, nor_3_out);
  // OR_Gate or_1 is placed but not wired
  // NOR_Gate nor_9 is placed but not wired
  // XOR_Gate xor_5 is placed but not wired
  // AND_Gate and_15 is placed but not wired
  // NAND_Gate nand_5 is placed but not wired
  // NOT_Gate not_7 is placed but not wired
endmodule

module Carry_adder_with_nice_input_output (
  input  Carry_In,
  input  [3:0] Input_A,
  input  [3:0] Input_B,
  output [3:0] Output,
  output Carry_Out
);

  _4_Bit_Carry_Adder u_4_bit_carry_adder_1 (
    .Carry_In(Carry_In), .Input_A1(Input_A[0]), .Input_B1(Input_B[0]), .Input_A2(Input_A[1]),
    .Input_B2(Input_B[1]), .Input_A3(Input_A[2]), .Input_B3(Input_B[2]), .Input_A4(Input_A[3]),
    .Input_B4(Input_B[3]), .out_10(Output[0]), .out_11(Output[1]), .out_12(Output[2]), .out_13(Output[3]),
    .out_14(Carry_Out));
endmodule

module main (
  input  Carry_in,
  input  [15:0] Input_A,
  input  [15:0] Input_B,
  input  Carry_in_2,
  input  [15:0] Input_A_2,
  input  [15:0] Input_B_2,
  output [15:0] Output,
  output [15:0] Output_2
);

  wire n16_bit_carry_look_ahead_adder_1_overflow_error, n16_bit_ripple_adder_1_overflow;

  Hex_Digit_Display hex_digit_display_1 (.value(Input_A[15:12]));  // open: dp
  Hex_Digit_Display hex_digit_display_2 (.value(Input_B[15:12]));  // open: dp
  Hex_Digit_Display hex_digit_display_3 (.value(Input_B_2[15:12]));  // open: dp
  Hex_Digit_Display hex_digit_display_4 (.value(Input_A[7:4]));  // open: dp
  Hex_Digit_Display hex_digit_display_5 (.value(Input_A[11:8]));  // open: dp
  Hex_Digit_Display hex_digit_display_6 (.value(Input_B[11:8]));  // open: dp
  Hex_Digit_Display hex_digit_display_7 (.value(Input_B[7:4]));  // open: dp
  Hex_Digit_Display hex_digit_display_8 (.value(Input_A_2[15:12]));  // open: dp
  Hex_Digit_Display hex_digit_display_9 (.value(Input_A_2[11:8]));  // open: dp
  Hex_Digit_Display hex_digit_display_10 (.value(Input_B_2[11:8]));  // open: dp
  Hex_Digit_Display hex_digit_display_11 (.value(Input_B_2[7:4]));  // open: dp
  Hex_Digit_Display hex_digit_display_12 (.value(Input_A[3:0]));  // open: dp
  _16_Bit_carry_look_ahead_adder u_16_bit_carry_look_ahead_adder_1 (
    .Input_A(Input_A), .Input_B(Input_B), .in_1(Carry_in), .out_4(Output),
    .OverFlow_Error(n16_bit_carry_look_ahead_adder_1_overflow_error));
  Hex_Digit_Display hex_digit_display_13 (.value(Input_B[3:0]));  // open: dp
  Hex_Digit_Display hex_digit_display_14 (.value(Input_A_2[3:0]));  // open: dp
  Hex_Digit_Display hex_digit_display_15 (.value(Input_A_2[7:4]));  // open: dp
  _16_bit_ripple_adder u_16_bit_ripple_adder_1 (
    .in_2(Input_A_2), .in_3(Input_B_2), .in_1(Carry_in_2), .out_4(Output_2),
    .OverFlow(n16_bit_ripple_adder_1_overflow));
  Hex_Digit_Display hex_digit_display_16 (.value(Input_B_2[3:0]));  // open: dp
  Hex_Digit_Display hex_digit_display_17 (.value(Output[15:12]));  // open: dp
  LED Overflow_Error (.in(n16_bit_carry_look_ahead_adder_1_overflow_error));
  LED Overflow_Error_2 (.in(n16_bit_ripple_adder_1_overflow));
  Hex_Digit_Display hex_digit_display_18 (.value(Output[7:4]));  // open: dp
  Hex_Digit_Display hex_digit_display_19 (.value(Output[11:8]));  // open: dp
  Hex_Digit_Display hex_digit_display_20 (.value(Output_2[15:12]));  // open: dp
  Hex_Digit_Display hex_digit_display_21 (.value(Output_2[11:8]));  // open: dp
  Hex_Digit_Display hex_digit_display_22 (.value(Output[3:0]));  // open: dp
  Hex_Digit_Display hex_digit_display_23 (.value(Output_2[3:0]));  // open: dp
  Hex_Digit_Display hex_digit_display_24 (.value(Output_2[7:4]));  // open: dp

  // Notes on the sheet:
  //   Carry Look Ahead Adder
  //   Carry Ripple Adder
  //   A (Hex)
  //   B (Hex)
  //   A (Hex)
  //   B (Hex)
  //   Sum (Hex)
  //   Sum (Hex)
endmodule

module _8_bit_Ripple_carry_adder (
  input  [7:0] A_Input,
  input  [7:0] B_input,
  input  Carry_In,
  output Overflow,
  output [7:0] Output_Sum
);

  wire adder_2_carry_out, adder_3_carry_out, adder_4_carry_out, adder_5_carry_out, adder_6_carry_out,
       adder_7_carry_out, adder_8_carry_out;

  Adder adder_1 (
    .Input_A(B_input[7]), .Input_B(A_Input[7]), .Carryin(adder_2_carry_out), .Carry_Out(Overflow),
    .Sum(Output_Sum[7]));
  Adder adder_2 (
    .Input_A(B_input[6]), .Input_B(A_Input[6]), .Carryin(adder_3_carry_out), .Carry_Out(adder_2_carry_out),
    .Sum(Output_Sum[6]));
  Adder adder_3 (
    .Input_A(B_input[5]), .Input_B(A_Input[5]), .Carryin(adder_4_carry_out), .Carry_Out(adder_3_carry_out),
    .Sum(Output_Sum[5]));
  Adder adder_4 (
    .Input_A(B_input[4]), .Input_B(A_Input[4]), .Carryin(adder_5_carry_out), .Carry_Out(adder_4_carry_out),
    .Sum(Output_Sum[4]));
  Adder adder_5 (
    .Input_A(B_input[3]), .Input_B(A_Input[3]), .Carryin(adder_6_carry_out), .Carry_Out(adder_5_carry_out),
    .Sum(Output_Sum[3]));
  Adder adder_6 (
    .Input_A(B_input[2]), .Input_B(A_Input[2]), .Carryin(adder_7_carry_out), .Carry_Out(adder_6_carry_out),
    .Sum(Output_Sum[2]));
  Adder adder_7 (
    .Input_A(B_input[1]), .Input_B(A_Input[1]), .Carryin(adder_8_carry_out), .Carry_Out(adder_7_carry_out),
    .Sum(Output_Sum[1]));
  Adder adder_8 (
    .Input_A(B_input[0]), .Input_B(A_Input[0]), .Carryin(Carry_In), .Carry_Out(adder_8_carry_out),
    .Sum(Output_Sum[0]));
endmodule

module Adder (
  input  Input_A,
  input  Input_B,
  input  Carryin,
  output Sum,
  output Carry_Out
);

  wire and_1_out, and_2_out, xor_1_out;

  xor xor_1 (xor_1_out, Input_A, Input_B);
  and and_1 (and_1_out, Input_A, Input_B);
  xor xor_2 (Sum, xor_1_out, Carryin);
  and and_2 (and_2_out, xor_1_out, Carryin);
  or or_1 (Carry_Out, and_2_out, and_1_out);
endmodule

module _16_bit_ripple_adder (
  input  in_1,
  input  [15:0] in_2,
  input  [15:0] in_3,
  output [15:0] out_4,
  output OverFlow
);

  wire n8_bit_ripple_carry_adder_1_overflow;

  _8_bit_Ripple_carry_adder u_8_bit_ripple_carry_adder_1 (
    .Output_Sum(out_4[7:0]), .Overflow(n8_bit_ripple_carry_adder_1_overflow), .Carry_In(in_1),
    .A_Input(in_3[7:0]), .B_input(in_2[7:0]));
  _8_bit_Ripple_carry_adder u_8_bit_ripple_carry_adder_2 (
    .Output_Sum(out_4[15:8]), .Overflow(OverFlow), .Carry_In(n8_bit_ripple_carry_adder_1_overflow),
    .A_Input(in_3[15:8]), .B_input(in_2[15:8]));
endmodule
